# Fritzing sketch potentiometer (saved by Fritzing 0.9.3b)

parts:
  Componente1 = Arduino Micro (Rev3)
  U1 = POT [package=alps_pot]
  S1 = Toggle Switch [package=THT]
  R1 = Resistor [tolerance=±5% resistance=10k package="2010 [SMD]"]

nets:
  N1: Componente1.GND, U1.E
  N2: Componente1.A1, S1.COM, R1.Pin_1
  N3: Componente1.A0, U1.S
  N4: U1.A, R1.Pin_0
